# Fritzing sketch GasSensor (saved by Fritzing 0.9.3b)
circuit board: 6cm x 5cm
breadboards: 1

parts:
  WeMos_D1_Mini1 = WeMos D1 Mini
  R1 = Resistor [tolerance=±5% resistance=10k package=THT]
  220V = screw terminal, 2 pins
  HLK-PM1 = HLK-PM01
  MQ-4 = female pin header, 4 pins [form="♀ (female)"]
  DHT22 = female pin header, 4 pins [form="♀ (female)"]

nets:
  5V: WeMos_D1_Mini1.5V, R1.Pin_0, HLK-PM1.+Vo, MQ-4.pin1, DHT22.pin1
  N1: WeMos_D1_Mini1.A0, MQ-4.pin4
  N2: WeMos_D1_Mini1.D4, R1.Pin_1, DHT22.pin2
  N3: WeMos_D1_Mini1.D7, MQ-4.pin3
  GND: WeMos_D1_Mini1.G, HLK-PM1.-Vo, MQ-4.pin2, DHT22.pin4
  N4: 220V.pin1, HLK-PM1.AC#1
  N5: 220V.pin2, HLK-PM1.AC#0
